# Fritzing sketch Fritzing Sketch Source File (saved by Fritzing 0.9.3b)
breadboards: 1

parts:
  Part1 = Arduino Uno (Rev3)
  R1 = Resistor [tolerance=±5% resistance=220 package="0805 [SMD]"]
  R2 = Resistor [tolerance=±5% resistance=220 package="0805 [SMD]"]
  LED2 = LED - 3mm [color="Red (633nm)" package="3 mm [THT]"]
  LED3 = LED - 3mm [color="Red (633nm)" package="3 mm [THT]"]
  J1 = Piezo Speaker
  Water_Level_Sensor1 = Water Level Sensor

nets:
  N1: Part1.A0, Water_Level_Sensor1.SIG
  GND: Part1.GND, LED2.cathode, LED3.cathode, J1.pin1, Water_Level_Sensor1.GND
  N2: Part1.D2, J1.pin2
  N3: Part1.D3_PWM, R1.Pin_0
  N4: Part1.D4, R2.Pin_0
  5V: Part1.5V, Water_Level_Sensor1.VCC
  N5: R1.Pin_1, LED3.anode
  N6: R2.Pin_1, LED2.anode

notes:
  Developed By Web Dev Fusion
  www.webdevfusion.com
  GND - Black
  5VC - Red
  GPIO - Blue

custom parts:
  Water Level Sensor: A water level sensor. This sensor operates at 3V to 5V. The Sig (signal) pin outputs an analogue signal that is in proportion to the amount of water in contact with the sensor.
